// Logisim project Last.circ as structural Verilog: 1 circuit, main circuit main
module main (
  input  in_1
);

  wire all_inter, and_3_out, and_4_out, and_6_out, and_7_out, and_8_out, cdm_16_1_p3, cdm_16_1_p4,
       cdm_16_1_p6, cdm_16_1_p7, cdm_16_1_p8, cdm_16_1_p9, cdm_16_1_p10, cdm_16_1_p11, cdm_16_1_p12,
       cdm_16_1_p13, cdm_16_1_p15, cdm_16_1_p16, clock, comparator_1_eq, comparator_2_eq, comparator_3_eq,
       comparator_4_eq, comparator_5_eq, comparator_6_eq, enter_inter, input_inter, keyboard_1_avail, mem,
       not_1_out, not_2_out, not_3_out, ozu_mem, program_mem, pzu_mem, read, word;
  wire [5:0] multiplexer_2_out, number_inter;
  wire [6:0] keyboard_1_data, register_2_q;
  wire [15:0] address_bus, bit_extender_1_out, cdm_16_1_p20, cdm_16_1_p21, counter_1_q, counter_2_q,
       data_bus, num_input, subtractor_1_out;

  // Probe on number_inter
  // Probe on cdm_16_1_p3
  // Probe on cdm_16_1_p4
  buf or_1 (all_inter, input_inter);  // OR_Gate
  // Probe on cdm_16_1_p7
  // Probe on cdm_16_1_p6
  // CdM_16 cdm_16_1: pin names not known; wires that end beside it: all_inter, number_inter, cdm_16_1_p3, cdm_16_1_p4, clock, cdm_16_1_p6, cdm_16_1_p7, cdm_16_1_p8, cdm_16_1_p9, cdm_16_1_p10, cdm_16_1_p11, cdm_16_1_p12, cdm_16_1_p13, cdm_16_1_p13, cdm_16_1_p15, cdm_16_1_p16, read, word, address_bus, cdm_16_1_p20, cdm_16_1_p21
  Clock clock_1 (.out(clock));
  // Probe on cdm_16_1_p9
  Multiplexer #(.width(6)) multiplexer_1 (
    .in0(multiplexer_2_out), .in1(6'b001000), .out(number_inter), .sel(input_inter));  // open: en
  Multiplexer #(.width(6)) multiplexer_2 (
    .in0({6{1'b0}}), .in1(6'b001001), .out(multiplexer_2_out), .sel(enter_inter));  // open: en
  and and_1 (program_mem, address_bus[8], address_bus[9], address_bus[10], address_bus[11], address_bus[12], address_bus[13], address_bus[14], address_bus[15], mem);
  // Probe on cdm_16_1_p8
  // Probe on cdm_16_1_p10
  and and_2 (ozu_mem, mem, ~program_mem);  // AND_Gate
  // Probe on cdm_16_1_p12
  // Probe on cdm_16_1_p11
  assign cdm_16_1_p21 = read ? data_bus : 16'bz;  // Controlled_Buffer controlled_buffer_1
  Decoder #(.disabled(0)) decoder_1 (.out0(pzu_mem), .out1(mem), .sel(cdm_16_1_p15), .en(cdm_16_1_p16));
  assign data_bus = not_1_out ? cdm_16_1_p20 : 16'bz;  // Controlled_Buffer controlled_buffer_2
  not not_1 (not_1_out, read);
  // Debugger debugger_1: pin names not known
  // RAM ram_1: pin names not known; wires that end beside it: address_bus, word, ozu_mem, clock, read, data_bus
  // ROM rom_1: pin names not known; wires that end beside it: address_bus, pzu_mem, word, data_bus
  // UART uart_1: pin names not known; wires that end beside it: clock, in_1, 1'b1
  Comparator comparator_1 (.a(address_bus[7:0]), .b({8{1'b0}}), .eq(comparator_1_eq));  // open: gt, lt
  // Probe on data_bus
  assign data_bus = and_3_out ? num_input : 16'bz;  // Controlled_Buffer controlled_buffer_3
  and and_3 (and_3_out, read, program_mem, comparator_1_eq);
  TTY tty_1 (.data(keyboard_1_data), .clk(clock), .clr(comparator_2_eq));  // open: we
  Keyboard #(.buflen(256)) keyboard_1 (.clk(clock), .avail(keyboard_1_avail), .data(keyboard_1_data));  // open: re, clr
  Comparator #(.width(7)) comparator_2 (.a(keyboard_1_data), .b(7'b0001010), .eq(comparator_2_eq));  // open: gt, lt
  Register #(.width(16)) register_1 (.D(bit_extender_1_out), .Q(num_input), .clk(input_inter));  // open: en, clr
  // Probe on keyboard_1_data
  Register #(.width(7)) register_2 (.D(keyboard_1_data), .Q(register_2_q), .clk(clock));  // open: en, clr
  Comparator #(.width(7)) comparator_3 (.a(register_2_q), .b({7{1'b0}}), .eq(comparator_3_eq));  // open: gt, lt
  assign bit_extender_1_out = {{9{1'b0}}, keyboard_1_data};  // Bit_Extender bit_extender_1
  // Probe on bit_extender_1_out
  and and_4 (and_4_out, clock, keyboard_1_avail);
  and and_5 (input_inter, and_4_out, and_6_out);
  and and_6 (and_6_out, ~comparator_3_eq, clock);  // AND_Gate
  // Probe on data_bus
  assign data_bus = and_7_out ? subtractor_1_out : 16'bz;  // Controlled_Buffer controlled_buffer_4
  and and_7 (and_7_out, read, program_mem, comparator_4_eq);
  Comparator comparator_4 (.a(address_bus[7:0]), .b(8'h2), .eq(comparator_4_eq));  // open: gt, lt
  Comparator #(.width(16)) comparator_5 (.a(16'h8), .b(bit_extender_1_out), .eq(comparator_5_eq));  // open: gt, lt
  Counter #(.width(16), .max('hffff)) counter_1 (
    .Q(counter_1_q), .clk(comparator_5_eq));  // open: load, D, count, carry, clr
  not not_2 (not_2_out, comparator_5_eq);
  not not_3 (not_3_out, comparator_6_eq);
  Comparator #(.width(16)) comparator_6 (.a({16{1'b0}}), .b(bit_extender_1_out), .eq(comparator_6_eq));  // open: gt, lt
  // Probe on subtractor_1_out
  Subtractor #(.width(16)) subtractor_1 (.a(counter_2_q), .b(counter_1_q), .out(subtractor_1_out));  // open: bin, bout
  Counter #(.width(16), .max('hffff)) counter_2 (.Q(counter_2_q), .clk(and_8_out));  // open: load, D, count, carry, clr
  and and_8 (and_8_out, not_2_out, not_3_out);
  Comparator #(.width(16)) comparator_7 (.a(num_input), .b(16'ha), .eq(enter_inter));  // open: gt, lt

  // Other names for the same wires on the sheet: address_bus_prog[7:0] = address_bus[7:0]

  // Notes on the sheet:
  //   СДЕЛАТЬ ЧТОБЫ РАБОТАЛ enter И НЕ УХОДИЛ СЧЕТЧИК В МИНУС
endmodule
