// Logisim project Mefefe.circ as structural Verilog: 1 circuit, main circuit main
// 1
module main (
);

  wire cdm16_1_p1, cdm16_1_p3, cdm16_1_p4, cdm16_1_p6, cdm16_1_p7, cdm16_1_p8, cdm16_1_p9, cdm16_1_p10,
       cdm16_1_p11, cdm16_1_p12, clock, debugger_1_p1, mem, not_1_out, read, select, uart_1_p6, uart_1_p7,
       word;
  wire [15:0] address_bus, cdm16_1_p17, cdm16_1_p18, data_bus;

  // Debugger debugger_1: pin names not known; wires that end beside it: debugger_1_p1, debugger_1_p1
  // Probe on cdm16_1_p3
  // Probe on cdm16_1_p4
  // Probe on cdm16_1_p6
  // Probe on cdm16_1_p7
  // cdm16 cdm16_1: pin names not known; wires that end beside it: cdm16_1_p1, 6'b000101, cdm16_1_p3, cdm16_1_p4, clock, cdm16_1_p6, cdm16_1_p7, cdm16_1_p8, cdm16_1_p9, cdm16_1_p10, cdm16_1_p11, cdm16_1_p12, mem, read, word, address_bus, cdm16_1_p17, cdm16_1_p18
  Clock clock_1 (.out(clock));
  // Probe on cdm16_1_p9
  // Probe on cdm16_1_p10
  // Probe on cdm16_1_p8
  Comparator #(.width(15)) comparator_1 (.a(address_bus[14:0]), .b(15'h7f80), .eq(select));  // open: gt, lt
  // Probe on cdm16_1_p11
  // Probe on cdm16_1_p12
  assign cdm16_1_p18 = read ? data_bus : 16'bz;  // Controlled_Buffer controlled_buffer_1
  assign data_bus = not_1_out ? cdm16_1_p17 : 16'bz;  // Controlled_Buffer controlled_buffer_2
  not not_1 (not_1_out, read);
  // UART uart_1: pin names not known; wires that end beside it: cdm16_1_p17[7:0], data_bus[7:0], cdm16_1_p1, clock, read, uart_1_p6, uart_1_p7
  // RAM ram_1: pin names not known; wires that end beside it: address_bus, word, mem, clock, read, data_bus
  LED led_1 (.in(uart_1_p6));
  and and_1 (uart_1_p7, select, mem);
endmodule
