// Logisim project Meow.circ as structural Verilog: 1 circuit, main circuit main
module main (
  output halted,
  output halted_2,
  output halted_3
);

  wire and_1_out, and_2_out, and_3_out, and_4_out, and_6_out, button_1_out, cdm_8e_1_p1, cdm_8e_1_p2,
       cdm_8e_1_p4, cdm_8e_1_p5, cdm_8e_1_p7, cdm_8e_1_p8, cdm_8e_1_p9, CI, code, data, data_read, is_F0,
       is_F1, mem, not_1_out, not_2_out, not_3_out, ram_sel_out, rd_wr_prime, uart_sel_out;
  wire [1:0] uart_status;
  wire [7:0] cdm_8e_1_p12, cdm_8e_1_p13, controlled_buffer_2_out, multiplexer_1_out, mux_out, uart_1_p1;
  wire [15:8] cdm_8e_1_p12_2;

  // Debugger debugger_1: pin names not known
  // Probe on cdm_8e_1_p1
  // Probe on cdm_8e_1_p2
  Clock clock_1 (.out(CI));
  // Probe on cdm_8e_1_p5
  // Probe on cdm_8e_1_p4
  // Probe on cdm_8e_1_p7
  Button button_1 (.out(button_1_out));
  Comparator comparator_1 (.a(cdm_8e_1_p12), .b(8'hf0), .eq(is_F0));  // open: gt, lt
  not not_1 (not_1_out, cdm_8e_1_p9);
  // Probe on cdm_8e_1_p8
  // CdM_8e cdm_8e_1: pin names not known; wires that end beside it: cdm_8e_1_p1, cdm_8e_1_p2, CI, cdm_8e_1_p4, cdm_8e_1_p5, button_1_out, cdm_8e_1_p7, cdm_8e_1_p8, cdm_8e_1_p9, mem, rd_wr_prime, {cdm_8e_1_p12_2, cdm_8e_1_p12}, cdm_8e_1_p13, mux_out, cdm_8e_1_p12[0], rd_wr_prime, cdm_8e_1_p13
  assign mux_out = rd_wr_prime ? controlled_buffer_2_out : 8'bz;  // Controlled_Buffer controlled_buffer_1
  Comparator comparator_2 (.a(cdm_8e_1_p12), .b(8'hf1), .eq(is_F1));  // open: gt, lt
  Decoder decoder_1 (.out0(code), .out1(data), .sel(cdm_8e_1_p9), .en(mem));
  assign controlled_buffer_2_out = not_2_out ? cdm_8e_1_p13 : 8'bz;  // Controlled_Buffer controlled_buffer_2
  not not_2 (not_2_out, rd_wr_prime);
  and and_1 (and_1_out, is_F0, not_1_out);
  and and_2 (and_2_out, is_F1, not_1_out);
  not not_3 (not_3_out, uart_sel_out);
  or uart_sel (uart_sel_out, and_1_out, and_2_out);
  and ram_sel (ram_sel_out, not_3_out, data);
  and and_3 (and_3_out, ram_sel_out, is_F0);
  ROM #(.addrWidth(16)) rom_1 (.addr({cdm_8e_1_p12_2, cdm_8e_1_p12}), .data(controlled_buffer_2_out), .sel(code));
  RAM #(.addrWidth(16)) ram_1 (
    .addr({cdm_8e_1_p12_2, cdm_8e_1_p12}), .data(controlled_buffer_2_out), .sel(data), .clk(CI),
    .ld(rd_wr_prime));  // open: clr
  // UART uart_1: pin names not known; wires that end beside it: uart_1_p1, cdm_8e_1_p13, uart_status[0], CI, rd_wr_prime, uart_status[1], and_3_out
  Multiplexer #(.width(8), .enable("false")) multiplexer_1 (
    .in0(controlled_buffer_2_out), .in1(uart_1_p1), .out(multiplexer_1_out), .sel(and_4_out));
  and and_4 (and_4_out, is_F0, data_read);
  and and_5 (data_read, data, rd_wr_prime);
  Multiplexer #(.width(8), .enable("false")) multiplexer_2 (
    .in0(multiplexer_1_out), .in1({{6{1'b0}}, uart_status}), .out(mux_out), .sel(and_6_out));
  and and_6 (and_6_out, is_F1, data_read);

  // Notes on the sheet:
  //   contents of rom_1 (hex, n*v repeats v):
  //   d0 f0 d1 48 a1 d1 45 a1 d1 4c a1 d1 4c a1 d1 4f a1 d1 20 a1 ee ed
endmodule
